// Logisim project Processeur.circ as structural Verilog: 31 circuits, main circuit EQUAL8BIT
module main (
  input  [2:0] SlctA,
  input  [2:0] SlctC,
  input  WE,
  input  [3:0] SlctOP,
  input  [2:0] SlctB,
  output [7:0] S,
  output Err
);

  wire clock_1_out;
  wire [7:0] bancregistre_1_r1, bancregistre_1_r2, bancregistre_1_r3, bancregistre_1_r4, bancregistre_1_r5,
       bancregistre_1_r6, bancregistre_1_r7, bancregistre_1_r8, multiplexer_1_out, multiplexer_2_out,
       undriven;

  Clock clock_1 (.out(clock_1_out));
  Multiplexer #(.select(3), .width(8)) multiplexer_1 (
    .in0(bancregistre_1_r1), .in1(bancregistre_1_r2), .in2(bancregistre_1_r3), .in3(bancregistre_1_r4),
    .in4(bancregistre_1_r5), .in5(bancregistre_1_r6), .in6(bancregistre_1_r7), .in7(bancregistre_1_r8),
    .out(multiplexer_1_out), .sel(SlctA));
  BancRegistre bancregistre_1 (
    .CLK(clock_1_out), .C(undriven), .sltC(SlctC), .WE(WE), .R1(bancregistre_1_r1), .R2(bancregistre_1_r2),
    .R3(bancregistre_1_r3), .R4(bancregistre_1_r4), .R5(bancregistre_1_r5), .R6(bancregistre_1_r6),
    .R7(bancregistre_1_r7), .R8(bancregistre_1_r8));
  Multiplexer #(.select(3), .width(8)) multiplexer_2 (
    .in0(bancregistre_1_r1), .in1(bancregistre_1_r2), .in2(bancregistre_1_r3), .in3(bancregistre_1_r4),
    .in4(bancregistre_1_r5), .in5(bancregistre_1_r6), .in6(bancregistre_1_r7), .in7(bancregistre_1_r8),
    .out(multiplexer_2_out), .sel(SlctB));
  ALU alu_1 (.A(multiplexer_1_out), .B(multiplexer_2_out), .slctOP(SlctOP), .Sortie(S), .Err(Err));
endmodule

module EQUAL (
  input  A,
  input  B,
  output S
);

  wire and_1_out, and_2_out, not_1_out, not_2_out;

  and and_1 (and_1_out, A, B);
  not not_1 (not_1_out, A);
  and and_2 (and_2_out, not_1_out, not_2_out);
  not not_2 (not_2_out, B);
  or or_1 (S, and_1_out, and_2_out);
endmodule

module DIFF (
  input  A,
  input  B,
  output S
);

  wire and_1_out, and_2_out, not_1_out, not_2_out, or_1_out;

  and and_1 (and_1_out, A, B);
  not not_1 (not_1_out, A);
  and and_2 (and_2_out, not_1_out, not_2_out);
  not not_2 (not_2_out, B);
  or or_1 (or_1_out, and_1_out, and_2_out);
  not not_3 (S, or_1_out);
endmodule

module INF (
  input  A,
  input  B,
  output S
);

  wire not_1_out;

  not not_1 (not_1_out, A);
  and and_1 (S, not_1_out, B);
endmodule

module INF_FULL (
  input  A,
  input  B,
  input  R_1,
  output S
);

  wire and_1_out, and_2_out, and_3_out, not_1_out;

  not not_1 (not_1_out, A);
  and and_1 (and_1_out, not_1_out, R_1);
  and and_2 (and_2_out, not_1_out, B);
  and and_3 (and_3_out, B, R_1);
  or or_1 (S, and_1_out, and_2_out, and_3_out);
endmodule

module SUP (
  input  A,
  input  B,
  output S
);

  wire not_1_out;

  not not_1 (not_1_out, A);
  and and_1 (S, not_1_out, B);
endmodule

module SUP_FULL (
  input  A,
  input  B,
  input  R_1,
  output S
);

  wire and_1_out, and_2_out, and_3_out, not_1_out;

  not not_1 (not_1_out, B);
  and and_1 (and_1_out, A, R_1);
  and and_2 (and_2_out, A, not_1_out);
  and and_3 (and_3_out, not_1_out, R_1);
  or or_1 (S, and_1_out, and_2_out, and_3_out);
endmodule

module EQUAL8BIT (
  input  [7:0] A,
  input  [7:0] B,
  output out_3
);

  wire equal_1_s, equal_2_s, equal_3_s, equal_4_s, equal_5_s, equal_6_s, equal_7_s, equal_8_s;

  EQUAL equal_1 (.A(A[0]), .B(B[0]), .S(equal_1_s));
  EQUAL equal_2 (.A(A[1]), .B(B[1]), .S(equal_2_s));
  EQUAL equal_3 (.A(A[2]), .B(B[2]), .S(equal_3_s));
  EQUAL equal_4 (.A(A[3]), .B(B[3]), .S(equal_4_s));
  EQUAL equal_5 (.A(A[4]), .B(B[4]), .S(equal_5_s));
  EQUAL equal_6 (.A(A[5]), .B(B[5]), .S(equal_6_s));
  EQUAL equal_7 (.A(A[6]), .B(B[6]), .S(equal_7_s));
  EQUAL equal_8 (.A(A[7]), .B(B[7]), .S(equal_8_s));
  and and_1 (out_3, equal_1_s, equal_2_s, equal_3_s, equal_4_s, equal_5_s, equal_6_s, equal_7_s, equal_8_s);
endmodule

module DIFF8BIT (
  input  [7:0] A,
  input  [7:0] B,
  output out_3
);

  wire diff_1_s, diff_2_s, diff_3_s, diff_4_s, diff_5_s, diff_6_s, diff_7_s, diff_8_s;

  DIFF diff_1 (.A(A[0]), .B(B[0]), .S(diff_1_s));
  DIFF diff_2 (.A(A[1]), .B(B[1]), .S(diff_2_s));
  DIFF diff_3 (.A(A[2]), .B(B[2]), .S(diff_3_s));
  DIFF diff_4 (.A(A[3]), .B(B[3]), .S(diff_4_s));
  DIFF diff_5 (.A(A[4]), .B(B[4]), .S(diff_5_s));
  DIFF diff_6 (.A(A[5]), .B(B[5]), .S(diff_6_s));
  DIFF diff_7 (.A(A[6]), .B(B[6]), .S(diff_7_s));
  DIFF diff_8 (.A(A[7]), .B(B[7]), .S(diff_8_s));
  or or_1 (out_3, diff_1_s, diff_2_s, diff_3_s, diff_4_s, diff_5_s, diff_6_s, diff_7_s, diff_8_s);
endmodule

module INF8BIT (
  input  [7:0] A,
  input  [7:0] B,
  output out_3
);

  wire inf_full_1_s, inf_full_2_s, inf_full_3_s, inf_full_4_s, inf_full_5_s, inf_full_6_s, inf_full_7_s;

  INF_FULL inf_full_1 (.A(A[0]), .B(B[0]), .R_1(1'b0), .S(inf_full_1_s));
  INF_FULL inf_full_2 (.A(A[1]), .B(B[1]), .R_1(inf_full_1_s), .S(inf_full_2_s));
  INF_FULL inf_full_3 (.A(A[2]), .B(B[2]), .R_1(inf_full_2_s), .S(inf_full_3_s));
  INF_FULL inf_full_4 (.A(A[3]), .B(B[3]), .R_1(inf_full_3_s), .S(inf_full_4_s));
  INF_FULL inf_full_5 (.A(A[4]), .B(B[4]), .R_1(inf_full_4_s), .S(inf_full_5_s));
  INF_FULL inf_full_6 (.A(A[5]), .B(B[5]), .R_1(inf_full_5_s), .S(inf_full_6_s));
  INF_FULL inf_full_7 (.A(A[6]), .B(B[6]), .R_1(inf_full_6_s), .S(inf_full_7_s));
  INF_FULL inf_full_8 (.A(A[7]), .B(B[7]), .R_1(inf_full_7_s), .S(out_3));
endmodule

module SUP8BIT (
  input  [7:0] A,
  input  [7:0] B,
  output out_3
);

  wire sup_full_1_s, sup_full_2_s, sup_full_3_s, sup_full_4_s, sup_full_5_s, sup_full_6_s, sup_full_7_s;

  SUP_FULL sup_full_1 (.A(A[0]), .B(B[0]), .R_1(1'b0), .S(sup_full_1_s));
  SUP_FULL sup_full_2 (.A(A[1]), .B(B[1]), .R_1(sup_full_1_s), .S(sup_full_2_s));
  SUP_FULL sup_full_3 (.A(A[2]), .B(B[2]), .R_1(sup_full_2_s), .S(sup_full_3_s));
  SUP_FULL sup_full_4 (.A(A[3]), .B(B[3]), .R_1(sup_full_3_s), .S(sup_full_4_s));
  SUP_FULL sup_full_5 (.A(A[4]), .B(B[4]), .R_1(sup_full_4_s), .S(sup_full_5_s));
  SUP_FULL sup_full_6 (.A(A[5]), .B(B[5]), .R_1(sup_full_5_s), .S(sup_full_6_s));
  SUP_FULL sup_full_7 (.A(A[6]), .B(B[6]), .R_1(sup_full_6_s), .S(sup_full_7_s));
  SUP_FULL sup_full_8 (.A(A[7]), .B(B[7]), .R_1(sup_full_7_s), .S(out_3));
endmodule

module ET (
  input  [7:0] A,
  input  [7:0] B,
  output [7:0] out_3
);

  assign out_3 = A & B;  // AND_Gate and_1, 8 bits wide
endmodule

module OU (
  input  [7:0] A,
  input  [7:0] B,
  output [7:0] out_3
);

  assign out_3 = A | B;  // OR_Gate or_1, 8 bits wide
endmodule

module XOU (
  input  [7:0] A,
  input  [7:0] B,
  output [7:0] out_3
);

  assign out_3 = A ^ B;  // XOR_Gate xor_1, 8 bits wide
endmodule

module LSL (
  input  [7:0] A,
  output [7:0] Sortie
);

  // NoConnect on A[7]

  assign Sortie = {A[6:0], 1'b0};
endmodule

module LSR (
  input  [7:0] A,
  output [7:0] Sortie
);

  // NoConnect on A[0]

  assign Sortie = {1'b0, A[7:1]};
endmodule

module ASR (
  input  [7:0] A,
  output [7:0] Sortie
);

  // NoConnect on A[0]

  assign Sortie = {{2{A[7]}}, A[6:1]};
endmodule

module R_OL (
  input  [7:0] A,
  output [7:0] Sortie
);


  assign Sortie = {A[6:0], A[7]};
endmodule

module R_OR (
  input  [7:0] A,
  output [7:0] Sortie
);


  assign Sortie = {A[0], A[7:1]};
endmodule

module add1bit (
  input  Re,
  input  A,
  input  B,
  output S,
  output Rs
);

  wire and_1_out, and_2_out, or_1_out, xor_1_out;

  xor xor_1 (xor_1_out, A, B);
  or or_1 (or_1_out, B, Re);
  xor xor_2 (S, xor_1_out, Re);
  and and_1 (and_1_out, or_1_out, A);
  or or_2 (Rs, and_1_out, and_2_out);
  and and_2 (and_2_out, B, Re);
endmodule

module ADD (
  input  [7:0] A,
  input  [7:0] B,
  output [7:0] S,
  output Er
);

  wire add1bit_1_rs, add1bit_2_rs, add1bit_3_rs, add1bit_4_rs, add1bit_5_rs, add1bit_6_rs, add1bit_7_rs;

  add1bit add1bit_1 (.Re(1'b0), .A(A[0]), .B(B[0]), .S(S[0]), .Rs(add1bit_1_rs));
  add1bit add1bit_2 (.Re(add1bit_1_rs), .A(A[1]), .B(B[1]), .S(S[1]), .Rs(add1bit_2_rs));
  add1bit add1bit_3 (.Re(add1bit_2_rs), .A(A[2]), .B(B[2]), .S(S[2]), .Rs(add1bit_3_rs));
  add1bit add1bit_4 (.Re(add1bit_3_rs), .A(A[3]), .B(B[3]), .S(S[3]), .Rs(add1bit_4_rs));
  add1bit add1bit_5 (.Re(add1bit_4_rs), .A(A[4]), .B(B[4]), .S(S[4]), .Rs(add1bit_5_rs));
  add1bit add1bit_6 (.Re(add1bit_5_rs), .A(A[5]), .B(B[5]), .S(S[5]), .Rs(add1bit_6_rs));
  add1bit add1bit_7 (.Re(add1bit_6_rs), .A(A[6]), .B(B[6]), .S(S[6]), .Rs(add1bit_7_rs));
  add1bit add1bit_8 (.Re(add1bit_7_rs), .A(A[7]), .B(B[7]), .S(S[7]), .Rs(Er));
endmodule

module CC2 (
  input  [7:0] A,
  output [7:0] S,
  output Err
);

  wire add_1_er;
  wire [7:0] not_1_out;

  assign not_1_out = ~A;  // NOT_Gate not_1, 8 bits wide
  ADD add_1 (.A(not_1_out), .B(8'h1), .S(S), .Er(add_1_er));
  // NoConnect on add_1_er
  EQUAL8BIT equal8bit_1 (.A(A), .B(8'h80), .out_3(Err));
endmodule

module SUB (
  input  [7:0] A,
  input  [7:0] B,
  output [7:0] R,
  output Er
);

  wire add_1_er, cc2_1_err;
  wire [7:0] cc2_1_s;

  CC2 cc2_1 (.A(B), .S(cc2_1_s), .Err(cc2_1_err));
  ADD add_1 (.A(A), .B(cc2_1_s), .S(R), .Er(add_1_er));
  or or_1 (Er, add_1_er, cc2_1_err);
endmodule

module BLOC_OP_COMP (
  input  [7:0] A,
  input  [1:0] SlctOP,
  input  [7:0] B,
  output [7:0] S
);

  wire diff8bit_1_out_3, equal8bit_1_out_3, inf8bit_1_out_3, sup8bit_1_out_3;

  EQUAL8BIT equal8bit_1 (.A(A), .B(B), .out_3(equal8bit_1_out_3));
  DIFF8BIT diff8bit_1 (.A(A), .B(B), .out_3(diff8bit_1_out_3));
  INF8BIT inf8bit_1 (.A(A), .B(B), .out_3(inf8bit_1_out_3));
  SUP8BIT sup8bit_1 (.A(A), .B(B), .out_3(sup8bit_1_out_3));
  Multiplexer #(.select(2)) multiplexer_1 (
    .in0(equal8bit_1_out_3), .in1(diff8bit_1_out_3), .in2(inf8bit_1_out_3), .in3(sup8bit_1_out_3),
    .out(S[0]), .sel(SlctOP));

  assign S[7:1] = {7{1'b0}};
endmodule

module BLOC_OP_LOG (
  input  [1:0] SlctOP,
  input  [7:0] A,
  input  [7:0] B,
  output [7:0] S
);

  wire [7:0] et_1_out_3, ou_1_out_3, xou_1_out_3;

  ET et_1 (.A(A), .B(B), .out_3(et_1_out_3));
  OU ou_1 (.A(A), .B(B), .out_3(ou_1_out_3));
  XOU xou_1 (.A(A), .B(B), .out_3(xou_1_out_3));
  Multiplexer #(.select(2), .width(8)) multiplexer_1 (
    .in0(et_1_out_3), .in1(et_1_out_3), .in2(ou_1_out_3), .in3(xou_1_out_3), .out(S), .sel(SlctOP));
endmodule

module BLOC_OP_ARI (
  input  [7:0] A,
  input  [1:0] SlctOP,
  input  [7:0] B,
  output [7:0] out_4,
  output Err
);

  wire add_1_er, sub_1_er;
  wire [7:0] add_1_s, sub_1_r;

  ADD add_1 (.A(A), .B(B), .S(add_1_s), .Er(add_1_er));
  SUB sub_1 (.A(B), .B(A), .R(sub_1_r), .Er(sub_1_er));
  or or_1 (Err, add_1_er, sub_1_er);
  Multiplexer #(.width(8)) multiplexer_1 (.in0(add_1_s), .in1(sub_1_r), .out(out_4), .sel(SlctOP[1]));
endmodule

module BLOC_OP_ROT (
  input  [7:0] A,
  input  [1:0] SlctOP,
  output [7:0] S
);

  wire [7:0] asr_1_sortie, lsl_1_sortie, lsr_1_sortie, r_ol_1_sortie;

  LSL lsl_1 (.A(A), .Sortie(lsl_1_sortie));
  LSR lsr_1 (.A(A), .Sortie(lsr_1_sortie));
  ASR asr_1 (.A(A), .Sortie(asr_1_sortie));
  R_OL r_ol_1 (.A(A), .Sortie(r_ol_1_sortie));
  Multiplexer #(.select(2), .width(8)) multiplexer_1 (
    .in0(lsl_1_sortie), .in1(lsr_1_sortie), .in2(asr_1_sortie), .in3(r_ol_1_sortie), .out(S), .sel(SlctOP));
endmodule

module ALU (
  input  [7:0] A,
  input  [7:0] B,
  input  [3:0] slctOP,
  output [7:0] Sortie,
  output Err
);

  wire [7:0] bloc_op_ari_1_out_4, bloc_op_comp_1_s, bloc_op_log_1_s, bloc_op_rot_1_s;

  BLOC_OP_LOG bloc_op_log_1 (.SlctOP(slctOP[3:2]), .A(A), .B(B), .S(bloc_op_log_1_s));
  BLOC_OP_COMP bloc_op_comp_1 (.A(A), .SlctOP(slctOP[3:2]), .B(B), .S(bloc_op_comp_1_s));
  BLOC_OP_ROT bloc_op_rot_1 (.A(A), .SlctOP(slctOP[3:2]), .S(bloc_op_rot_1_s));
  BLOC_OP_ARI bloc_op_ari_1 (.A(A), .SlctOP(slctOP[3:2]), .B(B), .out_4(bloc_op_ari_1_out_4), .Err(Err));
  Multiplexer #(.select(2), .width(8)) multiplexer_1 (
    .in0(bloc_op_log_1_s), .in1(bloc_op_comp_1_s), .in2(bloc_op_rot_1_s), .in3(bloc_op_ari_1_out_4),
    .out(Sortie), .sel(slctOP[1:0]));
endmodule

module REG1BIT (
  input  D,
  input  WE,
  input  CLK,
  output Q
);

  wire and_1_out;

  and and_1 (and_1_out, WE, CLK);
  D_Flip_Flop d_ff_1 (.D(D), .clk(and_1_out), .Q(Q));  // open: Qn, preset, reset
endmodule

module Registre (
  input  [7:0] D,
  input  WE,
  input  CLK,
  output [7:0] Q
);

  wire and_1_out;

  and and_1 (and_1_out, WE, CLK);
  D_Flip_Flop d_ff_1 (.D(D[0]), .clk(and_1_out), .Q(Q[0]));  // open: Qn, preset, reset
  D_Flip_Flop d_ff_2 (.D(D[1]), .clk(and_1_out), .Q(Q[1]));  // open: Qn, preset, reset
  D_Flip_Flop d_ff_3 (.D(D[2]), .clk(and_1_out), .Q(Q[2]));  // open: Qn, preset, reset
  D_Flip_Flop d_ff_4 (.D(D[3]), .clk(and_1_out), .Q(Q[3]));  // open: Qn, preset, reset
  D_Flip_Flop d_ff_5 (.D(D[4]), .clk(and_1_out), .Q(Q[4]));  // open: Qn, preset, reset
  D_Flip_Flop d_ff_6 (.D(D[5]), .clk(and_1_out), .Q(Q[5]));  // open: Qn, preset, reset
  D_Flip_Flop d_ff_7 (.D(D[6]), .clk(and_1_out), .Q(Q[6]));  // open: Qn, preset, reset
  D_Flip_Flop d_ff_8 (.D(D[7]), .clk(and_1_out), .Q(Q[7]));  // open: Qn, preset, reset
endmodule

module BancRegistre (
  input  CLK,
  input  [7:0] C,
  input  [2:0] sltC,
  input  WE,
  output [7:0] R1,
  output [7:0] R2,
  output [7:0] R3,
  output [7:0] R4,
  output [7:0] R5,
  output [7:0] R6,
  output [7:0] R7,
  output [7:0] R8
);

  wire decoder_1_out0, decoder_1_out1, decoder_1_out2, decoder_1_out3, decoder_1_out4, decoder_1_out5,
       decoder_1_out6, decoder_1_out7;

  Decoder #(.select(3)) decoder_1 (
    .out0(decoder_1_out0), .out1(decoder_1_out1), .out2(decoder_1_out2), .out3(decoder_1_out3),
    .out4(decoder_1_out4), .out5(decoder_1_out5), .out6(decoder_1_out6), .out7(decoder_1_out7), .sel(sltC),
    .en(WE));
  // NoConnect on C[7:1]
  Registre registre_1 (.D(C), .WE(decoder_1_out0), .CLK(CLK), .Q(R1));
  Registre registre_2 (.D(C), .WE(decoder_1_out1), .CLK(CLK), .Q(R2));
  Registre registre_3 (.D(C), .WE(decoder_1_out2), .CLK(CLK), .Q(R3));
  Registre registre_4 (.D(C), .WE(decoder_1_out3), .CLK(CLK), .Q(R4));
  Registre registre_5 (.D(C), .WE(decoder_1_out4), .CLK(CLK), .Q(R5));
  Registre registre_6 (.D(C), .WE(decoder_1_out5), .CLK(CLK), .Q(R6));
  Registre registre_7 (.D(C), .WE(decoder_1_out6), .CLK(CLK), .Q(R7));
  REG1BIT reg1bit_1 (.D(C[0]), .WE(decoder_1_out7), .CLK(CLK), .Q(R8[0]));

  assign R8[7:1] = {7{1'b0}};
endmodule
